// Logisim project Calculadora Digital.circ as structural Verilog
module somador (
  input  A1,
  input  A2,
  input  A3,
  input  B1,
  input  B2,
  input  B3,
  input  A0,
  input  B0,
  output Carry,
  output S1,
  output S2,
  output S3,
  output S0
);

  wire meio_somador_carry;

  meio_somador meio_somador (.A(A0), .B(B0), .Soma(S0), .Carry(meio_somador_carry));
  somador_3_bits somador_3_bits_1 (
    .A1(A1), .A2(A2), .A3(A3), .B1(B1), .B2(B2), .B3(B3), .Carry_in(meio_somador_carry), .Carry(Carry),
    .S1(S1), .S2(S2), .S3(S3));
endmodule

module multiplexador (
  input  in_1,
  input  in_2
);
endmodule

module meio_somador (
  input  A,
  input  B,
  output Soma,
  output Carry
);

  xor xor_1 (Soma, A, B);
  and and_1 (Carry, A, B);
endmodule

module subtrator (
  input  A1,
  input  A2,
  input  A3,
  input  B1,
  input  B2,
  input  B3,
  input  A0,
  input  B0,
  output Carry,
  output S1,
  output S2,
  output S0,
  output S3
);

  wire not_1_out, not_2_out, not_3_out, not_4_out, somador_completo_1_carry;

  somador_completo somador_completo_1 (.A(A0), .B(not_1_out), .Cin(1'b1), .Soma(S0), .Carry(somador_completo_1_carry));
  not not_1 (not_1_out, B0);
  not not_2 (not_2_out, B1);
  not not_3 (not_3_out, B2);
  not not_4 (not_4_out, B3);
  somador_3_bits somador_3_bits_1 (
    .A1(A1), .A2(A2), .A3(A3), .B1(not_2_out), .B2(not_3_out), .B3(not_4_out),
    .Carry_in(somador_completo_1_carry), .Carry(Carry), .S1(S1), .S2(S2), .S3(S3));
endmodule

module complemento_de_2 (
  input  B0,
  input  B1,
  input  B2,
  input  B3,
  output out_5,
  output out_6,
  output out_7,
  output out_8
);

  // NOT_Gate not_1 has open pins: in=B0, out=open
  // NOT_Gate not_2 has open pins: in=B1, out=open
  // NOT_Gate not_3 has open pins: in=B2, out=open
  // NOT_Gate not_4 has open pins: in=B3, out=open
  meio_somador meio_somador_1 ();  // open: A, B, Soma, Carry
endmodule

module somador_completo (
  input  A,
  input  B,
  input  Cin,
  output Soma,
  output Carry
);

  wire and_1_out, and_2_out, xor_1_out;

  xor xor_1 (xor_1_out, A, B);
  xor xor_2 (Soma, Cin, xor_1_out);
  and and_1 (and_1_out, xor_1_out, Cin);
  and and_2 (and_2_out, A, B);
  or or_1 (Carry, and_1_out, and_2_out);
endmodule

module somador_3_bits (
  input  A1,
  input  A2,
  input  A3,
  input  B1,
  input  B2,
  input  B3,
  input  Carry_in,
  output Carry,
  output S1,
  output S2,
  output S3
);

  wire somador_completo_2_carry, somador_completo_carry;

  somador_completo somador_completo (.A(A1), .B(B1), .Cin(Carry_in), .Soma(S1), .Carry(somador_completo_carry));
  somador_completo somador_completo_2 (
    .A(A2), .B(B2), .Cin(somador_completo_carry), .Soma(S2), .Carry(somador_completo_2_carry));
  somador_completo somador_completo_3 (.A(A3), .B(B3), .Cin(somador_completo_2_carry), .Soma(S3), .Carry(Carry));
endmodule

module comparador (
  input  B,
  input  A0,
  input  A1,
  input  A2,
  input  A3,
  output C0,
  output C1,
  output C2,
  output C3
);

  and and_1 (C0, B, A0);
  and and_2 (C1, B, A1);
  and and_3 (C2, B, A2);
  and and_4 (C3, B, A3);
endmodule

module multiplicador (
  input  B0,
  input  A0,
  input  A1,
  input  A2,
  input  A3,
  input  B1,
  input  B2,
  input  B3,
  output M0
);

  wire comparador_1_c1, comparador_1_c2, comparador_1_c3, comparador_2_c0, comparador_2_c1, comparador_2_c2;

  comparador comparador_1 (
    .B(B0), .A0(A0), .A1(A1), .A2(A2), .A3(A3), .C0(M0), .C1(comparador_1_c1), .C2(comparador_1_c2),
    .C3(comparador_1_c3));
  comparador comparador_2 (
    .B(B1), .A0(A0), .A1(A1), .A2(A2), .A3(A3), .C0(comparador_2_c0), .C1(comparador_2_c1),
    .C2(comparador_2_c2));  // open: C3
  comparador comparador_3 (.B(B2), .A0(A0), .A1(A1), .A2(A2), .A3(A3));  // open: C0, C1, C2, C3
  comparador comparador_4 (.B(B3), .A0(A0), .A1(A1), .A2(A2), .A3(A3));  // open: C0, C1, C2, C3
  somador somador_1 (
    .A1(comparador_1_c2), .A2(comparador_1_c3), .A3(1'b0), .B1(comparador_2_c1), .B2(comparador_2_c2),
    .B3(1'b0), .A0(comparador_1_c1), .B0(comparador_2_c0));  // open: Carry, S1, S2, S3, S0
endmodule
